# Fritzing sketch gesture controled robot RX (saved by Fritzing 0.9.5d)
breadboards: 1

parts:
  Part4 = Arduino Nano (Rev3.0) (ICSP)
  Part5 = NRF24L01+ Breakout Board
  L298N1 = L298N DC motor driver

nets:
  GND: Part4.GND, Part5.GND, L298N1.GND
  N1: Part4.D2, L298N1.IN1
  N2: Part4.D3, L298N1.IN2
  N3: Part4.D4, L298N1.IN3
  N4: Part4.D5, L298N1.ENA
  N5: Part4.D6, L298N1.IN4
  N6: Part4.D7, L298N1.ENB
  N7: Part4.D8, Part5.CS
  N8: Part4.D9, Part5.CE
  N9: Part4.D11/MOSI, Part5.MOSI
  N10: Part4.D12/MISO, Part5.MISO
  VIN: Part4.VIN, Part5.VCC, L298N1.5V
  N11: Part4.D13/SCK, Part5.SCK

custom parts:
  L298N DC motor driver: 2x DC motor driver with 78M05 positive voltage regulator (7..35 V) L298N: max 46 V, 2 A Set 5 V Enable jumper to enable 5 V regultor (needed for the L298N) and +5 V output at screw terminal or supply external +5 V at screw terminal Set ENA and/or ENB to +5 V to enable motor permanently or supply ENA and/or ENB with PWM signal IN1 and IN2 set rotation directory for motor A (OUT1/OUT2) IN2 and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
