# Fritzing sketch gesture controled robot TX (saved by Fritzing 0.9.5d)
breadboards: 1

parts:
  Part2 = Arduino Nano (Rev3.0) (ICSP)
  Part3 = NRF24L01+ Breakout Board

nets:
  GND: Part2.GND, Part3.GND
  N1: Part2.D8, Part3.CS
  N2: Part2.D9, Part3.CE
  N3: Part2.D11/MOSI, Part3.MOSI
  N4: Part2.D12/MISO, Part3.MISO
  VIN: Part2.VIN, Part3.VCC
  N5: Part2.D13/SCK, Part3.SCK
